# Fritzing sketch core-schematic (saved by Fritzing 0.8.7b)
breadboards: 1

parts:
  R1 = Resistor [tolerance=±5% resistance=560 package=THT]  # not connected
  R = Resistor [tolerance=±5% resistance=560 package=THT]
  R4 = Resistor [tolerance=±5% resistance=10k package=THT]
  S1 = Pushbutton [package="[THT]"]
  LED1 = LED - 5mm [color="Red (633nm)" package="5 mm [THT]"]
  LED2 = LED - 5mm [color="Green (560nm)" package="5 mm [THT]"]
  J1 = Piezo Speaker
  Part1 = Arduino Uno (Rev3)
  R3 = Resistor [tolerance=±5% resistance=560 package=THT]
  R5 = Photocell (LDR) [package=THT]
  R6 = Resistor [tolerance=±5% resistance=10k package=THT]
  R7 = Resistor [tolerance=±5% resistance=10k package=THT]
  R8 = Resistor [tolerance=±5% resistance=220 package=THT]
  Q1 = NPN-Transistor [package="TO92 [THT]"]

nets:
  N1: R.Pin_0, Part1.D3_PWM
  N2: R.Pin_1, LED2.anode
  N3: R4.Pin_0, Part1.5V, R6.Pin_1, R8.Pin_1, Q1.C
  N4: R4.Pin_1, Part1.A0, R5.pin_0
  N5: S1.Pin_1, S1.Pin_2, R6.Pin_0
  N6: S1.Pin_3, S1.Pin_4, LED1.cathode, LED2.cathode, J1.pin2, Part1.D13/SCK, Part1.GND, R5.pin_1, R7.Pin_1
  N7: LED1.anode, R3.Pin_1
  N8: J1.pin1, Part1.D6_PWM
  N9: Part1.A1, R7.Pin_0, Q1.E
  N10: Part1.D2, R3.Pin_0
  Probe A: R8.Pin_0
  Probe B: Q1.B
