# Fritzing sketch core-sketch (saved by Fritzing 0.8.7b)
breadboards: 1
stripboards: 1

parts:
  Part1 = Arduino Uno (Rev3)
  LED1 = LED - 5mm [color="Red (633nm)" package="5 mm [THT]"]
  LED2 = LED - 5mm [color="Green (565nm)" package="5 mm [THT]"]
  R2 = Resistor [tolerance=±5% resistance=560 package=THT]
  R3 = Resistor [tolerance=±5% resistance=560 package=THT]
  R4 = Resistor [tolerance=±5% resistance=560 package=THT]
  R5 = Resistor [tolerance=±5% resistance=560 package=THT]
  LED3 = LED - 5mm [color="Red (633nm)" package="5 mm [THT]"]
  LED4 = LED - 5mm [color="Green (560nm)" package="5 mm [THT]"]
  R6 = Photocell (LDR) [package=THT]
  R7 = Resistor [tolerance=±5% resistance=10k package=THT]
  R9 = Resistor [tolerance=±5% resistance=10k package=THT]
  S1 = Pushbutton [package="[THT]"]
  J2 = Piezo Speaker
  Q1 = NPN-Transistor [package="TO92 [THT]"]
  R10 = Resistor [tolerance=±5% resistance=220 package=THT]
  R11 = Resistor [tolerance=±5% resistance=10k package=THT]

nets:
  N1: Part1.A0, R6.pin_1, R7.Pin_0
  N2: Part1.A1, Q1.E, R11.Pin_1
  N3: Part1.D13/SCK, R9.Pin_1, S1.Pin_1, S1.Pin_2
  N4: Part1.GND, S1.Pin_3, S1.Pin_4, J2.pin1, R11.Pin_0
  N5: Part1.D2, R2.Pin_1, R4.Pin_1
  N6: Part1.D3_PWM, R3.Pin_1, R5.Pin_1
  N7: Part1.D6_PWM, J2.pin2
  N8: Part1.5V, R6.pin_0, R7.Pin_1, R9.Pin_0, Q1.C, R10.Pin_0
  N9: LED1.anode, R2.Pin_0, R4.Pin_0, LED3.anode
  N10: LED2.cathode, LED4.cathode
  N11: LED2.anode, R3.Pin_0, R5.Pin_0, LED4.anode

notes:
  Flood Sensor
